# Fritzing sketch DSN-VC288_DSN6000AUD (saved by Fritzing 0.9.3b)
circuit board: 7.31408cm x 2.60109cm
breadboards: 1

parts:
  IN- = female pin header, 1 pin [form="♀ (female)"]
  J2 = Camdenboss CTB0158-2 [part_number=CTB0158-2 package=THT]
  IN+ = female pin header, 1 pin [form="♀ (female)"]
  OUT+ = female pin header, 1 pin [form="♀ (female)"]
  J3 = Camdenboss CTB0158-2 [part_number=CTB0158-2 package=THT]
  AMP_BLACK = female pin header, 1 pin [form="♀ (female)"]
  AMP_RED = female pin header, 1 pin [form="♀ (female)"]
  VYELLOW = female pin header, 1 pin [form="♀ (female)"]
  VIN+ = female pin header, 1 pin [form="♀ (female)"]
  VIN- = female pin header, 1 pin [form="♀ (female)"]
  OUT- = female pin header, 1 pin [form="♀ (female)"]

nets:
  N1: IN-.pin1, J2.pin1, VIN-.pin1
  N2: J2.pin2, IN+.pin1, VIN+.pin1
  N3: OUT+.pin1, J3.pin1, VYELLOW.pin1
  N4: J3.pin2, AMP_RED.pin1
  N5: AMP_BLACK.pin1, OUT-.pin1
